// Logisim project zy1501_u201514514_何卓_cpu.circ as structural Verilog: 2 circuits, main circuit cpu
module cpu (
);

  wire ADDR, ALUA, and_1_out, and_2_out, and_3_out, and_4_out, and_5_out, and_6_out, and_8_out, beq, bgez,
       bne, \b指令成功跳转 , clk, comparator_1_eq, comparator_2_eq, comparator_3_eq, comparator_3_gt, conw_1_we,
       d_ff_1_qn, DM_DIN, equal, halt, IM, MEMread, MEMwrite, not_1_out, not_2_out, not_3_out, not_4_out,
       or_1_out, or_2_out, or_4_out, R2_num, RST, syscall;
  wire [1:0] ALUB, PC, R1_num, RF_W, W_num;
  wire [2:0] EXT;
  wire [3:0] conw_1_aluop, PC_28_31;
  wire [4:0] rd, registerfile_1_p4, registerfile_1_p5, registerfile_1_p6, rs, rt;
  wire [7:0] ram_1_data;
  wire [15:0] \总周期数 , \无条件分支指令数 , \有条件分支成功跳转 , \有条件分支指令数 ;
  wire [27:0] PC_q;
  wire [31:0] ALU, bit_extender_4_out, bit_extender_6_out, IMM0, IMM1, IMM2, IMM3, IMM5, multiplexer_1_out,
       multiplexer_2_out, multiplexer_4_out, multiplexer_5_out, multiplexer_6_out, PC_4, PCS,
       registerfile_1_p7, registerfile_1_p8, rom_1_data, S_EXT, SyscallOut;
  wire [31:8] ram_1_data_2;

  Button \u_总复位  (.out(RST));
  // Probe on not_1_out
  not not_1 (not_1_out, halt);
  D_Flip_Flop d_ff_1 (.clk(clk), .D(halt), .Qn(d_ff_1_qn), .preset(RST));  // open: Q, en, reset
  Clock clock_1 (.out(clk));
  Comparator #(.width(2)) comparator_1 (.a(PC), .b(2'b10), .eq(comparator_1_eq));  // open: gt, lt
  Comparator #(.width(2)) comparator_2 (.a(PC), .b(2'b11), .eq(comparator_2_eq));  // open: gt, lt
  Hex_Digit_Display hex_digit_display_1 (.value(SyscallOut[31:28]));  // open: dp
  Hex_Digit_Display hex_digit_display_2 (.value(SyscallOut[27:24]));  // open: dp
  Multiplexer #(.select(2), .width(32)) multiplexer_1 (
    .in0(PC_4), .in1(multiplexer_2_out), .in2({PC_28_31, S_EXT[25:0], 2'b00}), .in3(registerfile_1_p7),
    .out(multiplexer_1_out), .sel(PC));  // open: en
  Register #(.width(32)) u_PC (.D(multiplexer_1_out), .en(not_1_out), .Q({PC_28_31, PC_q}), .clk(clk), .clr(RST));
  Counter #(.width(16), .max('hffff)) counter_1 (
    .count(d_ff_1_qn), .Q(\总周期数 ), .clk(clk), .clr(RST));  // open: load, D, carry
  or or_1 (or_1_out, comparator_1_eq, comparator_2_eq);
  or or_2 (or_2_out, beq, bne, bgez);
  Hex_Digit_Display hex_digit_display_3 (.value(SyscallOut[23:20]));  // open: dp
  Hex_Digit_Display hex_digit_display_4 (.value(SyscallOut[19:16]));  // open: dp
  // Probe on PC
  Adder #(.width(32)) adder_1 (.a(32'h4), .b({PC_28_31, PC_q}), .out(PC_4));  // open: cin, cout
  Adder #(.width(32)) adder_2 (.a(S_EXT), .b({PC_28_31, PC_q}), .out(PCS));  // open: cin, cout
  not not_2 (not_2_out, halt);
  Hex_Digit_Display hex_digit_display_5 (.value(SyscallOut[15:12]));  // open: dp
  Hex_Digit_Display hex_digit_display_6 (.value(SyscallOut[11:8]));  // open: dp
  Multiplexer #(.width(32)) multiplexer_2 (
    .in0(PC_4), .in1(PCS), .out(multiplexer_2_out), .sel(\b指令成功跳转 ));  // open: en
  and and_1 (and_1_out, or_1_out, not_2_out);
  and and_2 (and_2_out, or_2_out, not_2_out);
  and and_3 (and_3_out, \b指令成功跳转 , not_2_out);
  Hex_Digit_Display hex_digit_display_7 (.value(SyscallOut[7:4]));  // open: dp
  Hex_Digit_Display hex_digit_display_8 (.value(SyscallOut[3:0]));  // open: dp
  // Probe on PC_28_31
  // Probe on EXT
  ROM #(.addrWidth(10), .dataWidth(32)) rom_1 (
    .addr(PC_q[11:2]), .data({rom_1_data[31:26], rs, rt, rd, rom_1_data[10:0]}));  // open: sel
  Counter #(.width(16), .max('hffff)) counter_2 (
    .count(and_1_out), .Q(\无条件分支指令数 ), .clk(clk), .clr(RST));  // open: load, D, carry
  Counter #(.width(16), .max('hffff)) counter_3 (
    .count(and_2_out), .Q(\有条件分支指令数 ), .clk(clk), .clr(RST));  // open: load, D, carry
  Counter #(.width(16), .max('hffff)) counter_4 (
    .count(and_3_out), .Q(\有条件分支成功跳转 ), .clk(clk), .clr(RST));  // open: load, D, carry
  Multiplexer #(.select(3), .width(32)) multiplexer_3 (
    .in0(IMM0), .in1(IMM1), .in2(IMM2), .in3(IMM3), .in4(32'ha), .in5(IMM5), .out(S_EXT), .sel(EXT));  // open: in6, in7, en
  // Probe on {rd, rom_1_data[10:0]}
  or or_3 (\b指令成功跳转 , and_4_out, and_5_out, and_6_out);
  // Probe on and_6_out
  // Probe on rom_1_data[5:0]
  // Probe on rom_1_data[31:26]
  // Probe on \总周期数 
  // Probe on \无条件分支指令数 
  // Probe on \有条件分支指令数 
  // Probe on \有条件分支成功跳转 
  and and_4 (and_4_out, beq, equal);
  // Probe on and_5_out
  and and_5 (and_5_out, bne, not_3_out);
  and and_6 (and_6_out, bgez, or_4_out);
  Multiplexer #(.width(32)) multiplexer_4 (
    .in0(registerfile_1_p7), .in1({PC_28_31, PC_q}), .out(multiplexer_4_out), .sel(ALUA));  // open: en
  ALU alu_1 (
    .AluOP(conw_1_aluop), .X(multiplexer_4_out), .Equal(equal), .Result(ALU), .Y(multiplexer_5_out));  // open: Signed_Overflow, Result_2, UnSigned_Overflow
  Multiplexer #(.select(2), .width(32)) multiplexer_5 (
    .in0(registerfile_1_p8), .in1(S_EXT), .in2(32'h4), .in3({32{1'b0}}), .out(multiplexer_5_out), .sel(ALUB));  // open: en
  // Probe on equal
  conw conw_1 (
    .OP(rom_1_data[31:26]), .FUNC(rom_1_data[5:0]), .PC(PC), .IM(IM), .R1_num(R1_num), .R2_num(R2_num),
    .W_num(W_num), .RF_DIN(RF_W), .EXT(EXT), .ALUA(ALUA), .ALUB(ALUB), .ADDR(ADDR), .DM_DIN(DM_DIN),
    .WE(conw_1_we), .ALUOP(conw_1_aluop), .memread(MEMread), .memwrite(MEMwrite), .syscall(syscall),
    .beq(beq), .bne(bne), .bgez(bgez));  // open: ALL
  assign IMM0 = {{16{rd[4]}}, {rd, rom_1_data[10:0]}};  // Bit_Extender bit_extender_1
  assign IMM1 = {{27{1'b0}}, rom_1_data[10:6]};  // Bit_Extender bit_extender_2
  assign IMM3 = {{6{1'b0}}, {rs, rt, rd, rom_1_data[10:0]}};  // Bit_Extender bit_extender_3
  not not_3 (not_3_out, equal);
  // Probe on conw_1_aluop
  // Probe on syscall
  assign bit_extender_4_out = {{14{rd[4]}}, {rd, rom_1_data[10:0], 2'b00}};  // Bit_Extender bit_extender_4
  Adder #(.width(32)) adder_3 (.a(32'h4), .b(bit_extender_4_out), .out(IMM2));  // open: cin, cout
  assign IMM5 = {{16{1'b0}}, {rd, rom_1_data[10:0]}};  // Bit_Extender bit_extender_5
  Multiplexer #(.select(2), .width(32)) multiplexer_6 (
    .in0(ALU), .in1({ram_1_data_2, ram_1_data}), .in2(bit_extender_6_out), .out(multiplexer_6_out), .sel(RF_W));  // open: in3, en
  // Probe on conw_1_we
  // Probe on conw_1_we
  Comparator #(.width(32)) comparator_3 (
    .a(ALU), .b({32{1'b0}}), .gt(comparator_3_gt), .eq(comparator_3_eq));  // open: lt
  // Probe on equal
  or or_4 (or_4_out, comparator_3_gt, comparator_3_eq);
  // RegisterFile registerfile_1: pin names not known; wires that end beside it: multiplexer_6_out, clk, conw_1_we, registerfile_1_p4, registerfile_1_p5, registerfile_1_p6, registerfile_1_p7, registerfile_1_p8
  Multiplexer #(.width(5)) multiplexer_7 (.in0(rt), .in1(5'b00100), .out(registerfile_1_p6), .sel(R2_num));  // open: en
  Multiplexer #(.select(2), .width(5)) multiplexer_8 (
    .in0(rd), .in1(rt), .in2({5{1'b1}}), .out(registerfile_1_p4), .sel(W_num));  // open: in3, en
  Multiplexer #(.select(2), .width(5)) multiplexer_9 (
    .in0(rs), .in1(rt), .in2(5'b00010), .out(registerfile_1_p5), .sel(R1_num));  // open: in3, en
  not not_4 (not_4_out, equal);
  // Probe on halt
  and and_7 (halt, syscall, equal);
  and and_8 (and_8_out, syscall, not_4_out);
  // Probe on registerfile_1_p4
  Register #(.width(32)) register_1 (.D(registerfile_1_p8), .en(and_8_out), .Q(SyscallOut), .clk(clk), .clr(RST));
  RAM #(.addrWidth(20), .dataWidth(32), .bus("separate")) ram_1 (
    .addr(ALU[19:0]), .din(registerfile_1_p8), .data({ram_1_data_2, ram_1_data}), .str(MEMwrite), .clk(clk),
    .ld(MEMread), .clr(RST));  // open: sel
  assign bit_extender_6_out = {{24{ram_1_data[7]}}, ram_1_data};  // Bit_Extender bit_extender_6

  // Notes on the sheet:
  //   数码管输出应该用寄存器锁存，否则显示数据只能一闪而过
  //   可以通过项目增加Logisim库的方式将前几次实验完成的电路作为子电路引入到本电路中使用
  //   指令存储器
  //   数码管输出
  //   contents of rom_1 (hex, n*v repeats v):
  //   20110001 8000c05 20110001 20120002 20130003 8000c09 20110001 20120002 20130003 8000c0d 20110001
  //   20120002 20130003 8000c11 20110001 20120002 20130003 c000cb8 20100001 20110001 118fc0 112020
  //   20020022 c 118882 12200001 8000c15 112020 20020022 c 20110001 118880 112020 20020022 c 12200001
  //   8000c1f 20110001 118fc0 112020 20020022 c 1188c3 112020 20020022 c 118903 112020 20020022 c 118903
  //   112020 20020022 c 118903 112020 20020022 c 118903 112020 20020022 c 118903 112020 20020022 c 118903
  //   112020 20020022 c 118903 112020 20020022 c 20100001 109fc0 139fc3 8021 2012000c 24160003 26100001
  //   3210000f 20080008 20090001 139900 2709825 132020 20020022 c 1094022 1500fff9 22100001 2018000f
  //   2188024 108700 20080008 20090001 139902 2709825 132021 20020022 c 1094022 1500fff9 108702 2c9b022
  //   12c00001 8000c50 4020 1084027 84400 3508ffff 82021 20020022 c 2010ffff 20110000 ae300000 22100001
  //   22310004 ae300000 22100001 22310004 ae300000 22100001 22310004 ae300000 22100001 22310004 ae300000
  //   22100001 22310004 ae300000 22100001 22310004 ae300000 22100001 22310004 ae300000 22100001 22310004
  //   ae300000 22100001 22310004 ae300000 22100001 22310004 ae300000 22100001 22310004 ae300000 22100001
  //   22310004 ae300000 22100001 22310004 ae300000 22100001 22310004 ae300000 22100001 22310004 ae300000
  //   22100001 22310004 22100001 8020 2011003c 8e130000 8e340000 274402a 11000002 ae330000 ae140000
  //   2231fffc 1611fff8 102020 20020022 c 22100004 2011003c 1611fff2 2002000a c 20100000 22100001 102020
  //   20020022 c 22100002 102020 20020022 c 22100003 102020 20020022 c 22100004 102020 20020022 c 22100005
  //   102020 20020022 c 22100006 102020 20020022 c 22100007 102020 20020022 c 22100008 102020 20020022
  //   20020022 c 3e00008
  //   总复位信号应将除ROM以外所有存储组件全部清零
  //   寄存器文件
endmodule

module conw (
  input  [5:0] OP,
  input  [5:0] FUNC,
  output [1:0] PC,
  output IM,
  output [1:0] R1_num,
  output R2_num,
  output [1:0] W_num,
  output [1:0] RF_DIN,
  output [2:0] EXT,
  output ALUA,
  output [1:0] ALUB,
  output ADDR,
  output DM_DIN,
  output WE,
  output [3:0] ALUOP,
  output [22:0] ALL,
  output memread,
  output memwrite,
  output syscall,
  output beq,
  output bne,
  output bgez
);

  wire and_1_out, and_2_out, and_3_out, and_4_out, and_5_out, and_6_out, and_7_out, and_8_out, and_9_out,
       and_10_out, and_11_out, and_13_out, and_14_out, comparator_1_eq, comparator_2_eq, comparator_3_eq,
       comparator_4_eq, comparator_5_eq, comparator_6_eq, comparator_7_eq, comparator_8_eq, comparator_9_eq,
       comparator_10_eq, comparator_11_eq, comparator_12_eq, comparator_13_eq, comparator_14_eq,
       comparator_15_eq, comparator_16_eq, comparator_17_eq, comparator_18_eq, comparator_19_eq,
       comparator_20_eq, comparator_21_eq, comparator_22_eq, comparator_27_eq, comparator_28_eq,
       comparator_29_eq, comparator_30_eq, comparator_31_eq, comparator_32_eq, comparator_33_eq,
       comparator_34_eq, comparator_35_eq, comparator_36_eq, comparator_37_eq, comparator_38_eq,
       comparator_39_eq, comparator_40_eq, LB, LW;
  wire [22:0] multiplexer_1_out, multiplexer_2_out, multiplexer_3_out, multiplexer_4_out, multiplexer_5_out,
       multiplexer_6_out, multiplexer_7_out, multiplexer_8_out, multiplexer_9_out, multiplexer_10_out,
       multiplexer_11_out, multiplexer_12_out, multiplexer_13_out, multiplexer_14_out, multiplexer_15_out,
       multiplexer_16_out, multiplexer_17_out, multiplexer_18_out, multiplexer_19_out, multiplexer_20_out,
       multiplexer_21_out, multiplexer_22_out, multiplexer_23_out, multiplexer_24_out, multiplexer_25_out,
       multiplexer_26_out, multiplexer_27_out, multiplexer_28_out, or_1_out, or_2_out, or_3_out, or_4_out,
       or_5_out;

  Comparator #(.width(6)) comparator_1 (.a(OP), .b({6{1'b0}}), .eq(comparator_1_eq));  // open: gt, lt
  Comparator #(.width(6)) comparator_2 (.a(FUNC), .b(6'b100000), .eq(comparator_2_eq));  // open: gt, lt
  Comparator #(.width(6)) comparator_3 (.a(OP), .b(6'b001000), .eq(comparator_3_eq));  // open: gt, lt
  Comparator #(.width(6)) comparator_4 (.a(OP), .b(6'b001001), .eq(comparator_4_eq));  // open: gt, lt
  Comparator #(.width(6)) comparator_5 (.a(OP), .b({6{1'b0}}), .eq(comparator_5_eq));  // open: gt, lt
  Comparator #(.width(6)) comparator_6 (.a(FUNC), .b(6'b100001), .eq(comparator_6_eq));  // open: gt, lt
  Comparator #(.width(6)) comparator_7 (.a(OP), .b({6{1'b0}}), .eq(comparator_7_eq));  // open: gt, lt
  Comparator #(.width(6)) comparator_8 (.a(FUNC), .b(6'b100100), .eq(comparator_8_eq));  // open: gt, lt
  Comparator #(.width(6)) comparator_9 (.a(OP), .b(6'b001100), .eq(comparator_9_eq));  // open: gt, lt
  Comparator #(.width(6)) comparator_10 (.a(OP), .b({6{1'b0}}), .eq(comparator_10_eq));  // open: gt, lt
  Comparator #(.width(6)) comparator_11 (.a(FUNC), .b({6{1'b0}}), .eq(comparator_11_eq));  // open: gt, lt
  Comparator #(.width(6)) comparator_12 (.a(OP), .b({6{1'b0}}), .eq(comparator_12_eq));  // open: gt, lt
  Comparator #(.width(6)) comparator_13 (.a(FUNC), .b(6'b000011), .eq(comparator_13_eq));  // open: gt, lt
  Comparator #(.width(6)) comparator_14 (.a(OP), .b({6{1'b0}}), .eq(comparator_14_eq));  // open: gt, lt
  Comparator #(.width(6)) comparator_15 (.a(FUNC), .b(6'b000010), .eq(comparator_15_eq));  // open: gt, lt
  Comparator #(.width(6)) comparator_16 (.a(OP), .b({6{1'b0}}), .eq(comparator_16_eq));  // open: gt, lt
  Comparator #(.width(6)) comparator_17 (.a(FUNC), .b(6'b100010), .eq(comparator_17_eq));  // open: gt, lt
  Comparator #(.width(6)) comparator_18 (.a(OP), .b({6{1'b0}}), .eq(comparator_18_eq));  // open: gt, lt
  Comparator #(.width(6)) comparator_19 (.a(FUNC), .b(6'b100101), .eq(comparator_19_eq));  // open: gt, lt
  Comparator #(.width(6)) comparator_20 (.a(OP), .b(6'b001101), .eq(comparator_20_eq));  // open: gt, lt
  Comparator #(.width(6)) comparator_21 (.a(OP), .b({6{1'b0}}), .eq(comparator_21_eq));  // open: gt, lt
  Comparator #(.width(6)) comparator_22 (.a(FUNC), .b(6'b100111), .eq(comparator_22_eq));  // open: gt, lt
  Comparator #(.width(6)) comparator_23 (.a(OP), .b(6'b100011), .eq(LW));  // open: gt, lt
  Comparator #(.width(6)) comparator_24 (.a(OP), .b(6'b101011), .eq(memwrite));  // open: gt, lt
  Comparator #(.width(6)) comparator_25 (.a(OP), .b(6'b000100), .eq(beq));  // open: gt, lt
  Comparator #(.width(6)) comparator_26 (.a(OP), .b(6'b000101), .eq(bne));  // open: gt, lt
  Comparator #(.width(6)) comparator_27 (.a(OP), .b({6{1'b0}}), .eq(comparator_27_eq));  // open: gt, lt
  Comparator #(.width(6)) comparator_28 (.a(FUNC), .b(6'b101010), .eq(comparator_28_eq));  // open: gt, lt
  Comparator #(.width(6)) comparator_29 (.a(OP), .b(6'b001010), .eq(comparator_29_eq));  // open: gt, lt
  Comparator #(.width(6)) comparator_30 (.a(OP), .b({6{1'b0}}), .eq(comparator_30_eq));  // open: gt, lt
  Comparator #(.width(6)) comparator_31 (.a(FUNC), .b(6'b101011), .eq(comparator_31_eq));  // open: gt, lt
  Comparator #(.width(6)) comparator_32 (.a(OP), .b(6'b000010), .eq(comparator_32_eq));  // open: gt, lt
  Comparator #(.width(6)) comparator_33 (.a(OP), .b(6'b000011), .eq(comparator_33_eq));  // open: gt, lt
  Comparator #(.width(6)) comparator_34 (.a(OP), .b({6{1'b0}}), .eq(comparator_34_eq));  // open: gt, lt
  Comparator #(.width(6)) comparator_35 (.a(FUNC), .b(6'b001000), .eq(comparator_35_eq));  // open: gt, lt
  Comparator #(.width(6)) comparator_36 (.a(OP), .b({6{1'b0}}), .eq(comparator_36_eq));  // open: gt, lt
  Comparator #(.width(6)) comparator_37 (.a(FUNC), .b(6'b001100), .eq(comparator_37_eq));  // open: gt, lt
  Comparator #(.width(6)) comparator_38 (.a(OP), .b({6{1'b0}}), .eq(comparator_38_eq));  // open: gt, lt
  Comparator #(.width(6)) comparator_39 (.a(FUNC), .b(6'b100011), .eq(comparator_39_eq));  // open: gt, lt
  Comparator #(.width(6)) comparator_40 (.a(OP), .b(6'b001110), .eq(comparator_40_eq));  // open: gt, lt
  Comparator #(.width(6)) comparator_41 (.a(OP), .b(6'b100000), .eq(LB));  // open: gt, lt
  Comparator #(.width(6)) comparator_42 (.a(OP), .b(6'b000001), .eq(bgez));  // open: gt, lt
  and and_1 (and_1_out, comparator_5_eq, comparator_6_eq);
  and and_2 (and_2_out, comparator_7_eq, comparator_8_eq);
  and and_3 (and_3_out, comparator_10_eq, comparator_11_eq);
  and and_4 (and_4_out, comparator_12_eq, comparator_13_eq);
  and and_5 (and_5_out, comparator_14_eq, comparator_15_eq);
  and and_6 (and_6_out, comparator_16_eq, comparator_17_eq);
  and and_7 (and_7_out, comparator_18_eq, comparator_19_eq);
  and and_8 (and_8_out, comparator_21_eq, comparator_22_eq);
  and and_9 (and_9_out, comparator_27_eq, comparator_28_eq);
  and and_10 (and_10_out, comparator_30_eq, comparator_31_eq);
  and and_11 (and_11_out, comparator_34_eq, comparator_35_eq);
  and and_12 (syscall, comparator_36_eq, comparator_37_eq);
  and and_13 (and_13_out, comparator_38_eq, comparator_39_eq);
  and and_14 (and_14_out, comparator_1_eq, comparator_2_eq);
  Multiplexer #(.width(23)) multiplexer_1 (
    .in0({23{1'b0}}), .in1(23'h949a), .out(multiplexer_1_out), .sel(comparator_40_eq));  // open: en
  Multiplexer #(.width(23)) multiplexer_2 (
    .in0({23{1'b0}}), .in1(23'hc0d5), .out(multiplexer_2_out), .sel(LB));  // open: en
  Multiplexer #(.width(23)) multiplexer_3 (
    .in0({23{1'b0}}), .in1(23'h200986), .out(multiplexer_3_out), .sel(bgez));  // open: en
  Multiplexer #(.width(23)) multiplexer_4 (
    .in0({23{1'b0}}), .in1(23'h15), .out(multiplexer_4_out), .sel(and_14_out));  // open: en
  Multiplexer #(.width(23)) multiplexer_5 (
    .in0({23{1'b0}}), .in1(23'h8095), .out(multiplexer_5_out), .sel(comparator_3_eq));  // open: en
  Multiplexer #(.width(23)) multiplexer_6 (
    .in0({23{1'b0}}), .in1(23'h8095), .out(multiplexer_6_out), .sel(comparator_4_eq));  // open: en
  Multiplexer #(.width(23)) multiplexer_7 (
    .in0({23{1'b0}}), .in1(23'h15), .out(multiplexer_7_out), .sel(and_1_out));  // open: en
  Multiplexer #(.width(23)) multiplexer_8 (
    .in0({23{1'b0}}), .in1(23'h17), .out(multiplexer_8_out), .sel(and_2_out));  // open: en
  Multiplexer #(.width(23)) multiplexer_9 (
    .in0({23{1'b0}}), .in1(23'h9497), .out(multiplexer_9_out), .sel(comparator_9_eq));  // open: en
  Multiplexer #(.width(23)) multiplexer_10 (
    .in0({23{1'b0}}), .in1(23'h40490), .out(multiplexer_10_out), .sel(and_3_out));  // open: en
  Multiplexer #(.width(23)) multiplexer_11 (
    .in0({23{1'b0}}), .in1(23'h40491), .out(multiplexer_11_out), .sel(and_4_out));  // open: en
  Multiplexer #(.width(23)) multiplexer_12 (
    .in0({23{1'b0}}), .in1(23'h40492), .out(multiplexer_12_out), .sel(and_5_out));  // open: en
  Multiplexer #(.width(23)) multiplexer_13 (
    .in0({23{1'b0}}), .in1(23'h16), .out(multiplexer_13_out), .sel(and_6_out));  // open: en
  Multiplexer #(.width(23)) multiplexer_14 (
    .in0({23{1'b0}}), .in1(23'h18), .out(multiplexer_14_out), .sel(and_7_out));  // open: en
  Multiplexer #(.width(23)) multiplexer_15 (
    .in0({23{1'b0}}), .in1(23'h9498), .out(multiplexer_15_out), .sel(comparator_20_eq));  // open: en
  Multiplexer #(.width(23)) multiplexer_16 (
    .in0({23{1'b0}}), .in1(23'h1a), .out(multiplexer_16_out), .sel(and_8_out));  // open: en
  Multiplexer #(.width(23)) multiplexer_17 (
    .in0({23{1'b0}}), .in1(23'ha0d5), .out(multiplexer_17_out), .sel(LW));  // open: en
  Multiplexer #(.width(23)) multiplexer_18 (
    .in0({23{1'b0}}), .in1(23'he5), .out(multiplexer_18_out), .sel(memwrite));  // open: en
  Multiplexer #(.width(23)) multiplexer_19 (
    .in0({23{1'b0}}), .in1(23'h200806), .out(multiplexer_19_out), .sel(beq));  // open: en
  Multiplexer #(.width(23)) multiplexer_20 (
    .in0({23{1'b0}}), .in1(23'h200806), .out(multiplexer_20_out), .sel(bne));  // open: en
  Multiplexer #(.width(23)) multiplexer_21 (
    .in0({23{1'b0}}), .in1(23'h1b), .out(multiplexer_21_out), .sel(and_9_out));  // open: en
  Multiplexer #(.width(23)) multiplexer_22 (
    .in0({23{1'b0}}), .in1(23'h809b), .out(multiplexer_22_out), .sel(comparator_29_eq));  // open: en
  Multiplexer #(.width(23)) multiplexer_23 (
    .in0({23{1'b0}}), .in1(23'h1c), .out(multiplexer_23_out), .sel(and_10_out));  // open: en
  Multiplexer #(.width(23)) multiplexer_24 (
    .in0({23{1'b0}}), .in1(23'h400c00), .out(multiplexer_24_out), .sel(comparator_32_eq));  // open: en
  Multiplexer #(.width(23)) multiplexer_25 (
    .in0({23{1'b0}}), .in1(23'h410f15), .out(multiplexer_25_out), .sel(comparator_33_eq));  // open: en
  Multiplexer #(.width(23)) multiplexer_26 (
    .in0({23{1'b0}}), .in1(23'h600000), .out(multiplexer_26_out), .sel(and_11_out));  // open: en
  Multiplexer #(.width(23)) multiplexer_27 (
    .in0({23{1'b0}}), .in1(23'ha1086), .out(multiplexer_27_out), .sel(syscall));  // open: en
  Multiplexer #(.width(23)) multiplexer_28 (
    .in0({23{1'b0}}), .in1(23'h16), .out(multiplexer_28_out), .sel(and_13_out));  // open: en
  assign or_1_out = multiplexer_4_out | multiplexer_5_out | multiplexer_6_out | multiplexer_7_out;  // OR_Gate or_1, 23 bits wide
  assign or_2_out = multiplexer_14_out | multiplexer_15_out | multiplexer_16_out | multiplexer_17_out | multiplexer_18_out | multiplexer_19_out;  // OR_Gate or_2, 23 bits wide
  assign or_3_out = multiplexer_8_out | multiplexer_9_out | multiplexer_10_out | multiplexer_11_out | multiplexer_12_out | multiplexer_13_out;  // OR_Gate or_3, 23 bits wide
  assign or_4_out = multiplexer_20_out | multiplexer_21_out | multiplexer_22_out | multiplexer_23_out | multiplexer_24_out | multiplexer_25_out;  // OR_Gate or_4, 23 bits wide
  assign or_5_out = multiplexer_26_out | multiplexer_27_out | multiplexer_28_out | multiplexer_1_out | multiplexer_2_out | multiplexer_3_out;  // OR_Gate or_5, 23 bits wide
  assign {ALL[22:7], ADDR, ALL[5:0]} = or_1_out | or_3_out | or_2_out | or_4_out | or_5_out;  // OR_Gate or_6, 23 bits wide
  or or_7 (memread, LW, LB);

  assign ALL[6] = ADDR;
  assign ALUA = ALL[9];
  assign ALUB = ALL[8:7];
  assign ALUOP = ALL[3:0];
  assign DM_DIN = ALL[5];
  assign EXT = ALL[12:10];
  assign IM = ALL[20];
  assign PC = ALL[22:21];
  assign R1_num = ALL[19:18];
  assign R2_num = ALL[17];
  assign RF_DIN = ALL[14:13];
  assign W_num = ALL[16:15];
  assign WE = ALL[4];

  // Other names for the same wires on the sheet: _23位[22:0] = {ALL[22:7], ADDR, ALL[5:0]}; SW = memwrite
endmodule
